# Fritzing sketch RedundantPower (saved by Fritzing 0.9.2b)
circuit board: 4cm x 5cm
breadboards: 1

parts:
  VCC1 = Battery
  VCC2 = Battery
  IC1 = Voltage Regulator [part_number=MBR1545CT package=to-220-alt]
  J3-Fuse = rounded female pin header, 3 pins [form="♀ (female rounded)"]
  VCC2_2 = rounded female pin header, 2 pins [form="♀ (female rounded)"]
  Pwr_out = rounded female pin header, 2 pins [form="♀ (female rounded)"]
  J2-sw = rounded female pin header, 2 pins [form="♀ (female rounded)"]
  VCC1_2 = rounded female pin header, 2 pins [form="♀ (female rounded)"]

nets:
  N1: VCC1.-, VCC2.-, VCC2_2.pin2, Pwr_out.pin1, VCC1_2.pin2
  N2: VCC1.+, IC1.OUT, VCC1_2.pin1
  N3: VCC2.+, IC1.IN, VCC2_2.pin1
  N4: IC1.GND, J3-Fuse.pin3
  N5: J3-Fuse.pin1, J2-sw.pin2
  N6: Pwr_out.pin2, J2-sw.pin1

notes:
  2019 Izzy Multi-Power
  Switch
  PwrOut
  Fuse
  VCC1
  Sw
  Pwr Out
  MBR1545
  VCC2
  +
  gnd -
